# Fritzing sketch sdp (saved by Fritzing 0.7.12b)
perfboards: 1

parts:
  Arduino1 = Arduino
  U1 = atmega328 [package=dip]
  XTAL1 = Crystal [frequency="16 Mhz" package=SMD]
  C1 = Ceramic Disk Capacitor [package=THT]
  C2 = Ceramic Disk Capacitor [package=THT]
  R1 = Resistor [tolerance=±5% resistance=10k package=THT]
  Part1 = Bluetooth Mate Silver
  IC1 = L293D [package=THT]
  IC2 = L293D [package=THT]
  VCC1 = Battery
  VCC2 = 4 x AAA Battery Mount

nets:
  N1: Arduino1.D11, IC1.In_1
  N2: Arduino1.D10, IC1.In_2
  N3: Arduino1.D6, IC1.In_4
  N4: Arduino1.D5, IC1.In_3
  N5: Arduino1.RST, U1.RESET, R1.Pin_0
  3V3: Arduino1.3V3, Part1.VCC
  +5V: Arduino1.+5V, U1.VCC, U1.AVCC, R1.Pin_1, IC1.Enable_1, IC1.Enable_2, IC1.+V, IC2.Enable_1, IC2.Enable_2, IC2.+V
  GND: Arduino1.GND, U1.GND, C1.pin_1, C2.pin_0, Part1.CTS_5V, Part1.GND, IC1.0V, IC2.0V, VCC1.-, VCC2.-
  N6: Arduino1.VIN, VCC2.+
  N7: U1.D0_(RX), Part1.TX_5V
  N8: U1.D1_(TX), Part1.RTS_5V, Part1.RX_5V
  N9: U1.XLAT1, XTAL1.pin_1, C2.pin_1
  N10: U1.XLAT2, XTAL1.pin_0, C1.pin_0
  N11: U1.D5_(PWM), IC2.In_3
  N12: U1.D6_(PWM), IC2.In_4
  N13: U1.D10_(PWM), IC2.In_2
  N14: U1.D11_(PWM), IC2.In_1
  N15: IC1.+Vmotor, IC2.+Vmotor, VCC1.+
